# Fritzing sketch circuito micro (saved by Fritzing 1.0.4)
breadboards: 1

parts:
  Componente1 = Arduino Mega ADK (Rev3)
  Componente2 = Adafruit MCP4725 Breakout Board - 12-Bit DAC [part_number="Adafruit #935"]
  R1 = Resistor [tolerance=±5% power=0.25W resistance=15k package=THT]  # not connected
  R2 = Resistor [tolerance=±5% power=0.25W resistance=15k package=THT]
  U1 = LM 358 Dual Op-Amp [package="DIP8 [THT]"]
  R3 = Resistor [tolerance=±5% power=0.25W resistance=15k package=THT]
  R5 = Resistor [tolerance=±5% power=0.25W resistance=15k package=THT]
  R6 = Resistor [tolerance=±5% power=0.25W resistance=15k package=THT]
  R7 = Resistor [tolerance=±5% power=0.25W resistance=15k package=THT]
  R8 = Resistor [tolerance=±5% power=0.25W resistance=15k package=THT]
  R9 = Resistor [tolerance=±5% power=0.25W resistance=15k package=THT]
  RE1 = KY-040 Rotary encoder [package=THT]
  RE2 = KY-040 Rotary encoder [package=THT]
  LCD1 = 2.8 Zoll LCD IL19341 [mpn=MSP2807 part_number=MSP2807]

nets:
  N1: Componente1.D21/SCL, Componente2.SCL
  N2: Componente1.D20/SDA, Componente2.SDA
  N3: Componente1.D10_PWM, LCD1.pin3
  N4: Componente1.D9_PWM, LCD1.pin5
  N5: Componente1.D8_PWM, LCD1.pin4
  GND: Componente1.GND, Componente2.GND, Componente2.A0, R2.Pin_1, R5.Pin_1, RE1.GND, RE2.GND, LCD1.pin2
  VCC: Componente1.5V, Componente2.VDD, RE1.Vcc, RE2.Vcc, LCD1.pin1, LCD1.pin8
  N6: Componente1.D31, RE1.DT
  N7: Componente1.D35, RE2.DT
  N8: Componente1.D39, RE2.CLK
  N9: Componente1.D43, RE1.CLK
  N10: Componente1.D49, RE1.SW
  N11: Componente1.D50/MISO, LCD1.pin9
  N12: Componente1.D51/MOSI, LCD1.pin6
  N13: Componente1.D52/SCK, LCD1.pin7
  N14: Componente2.VOUT, R3.Pin_0
  N15: R2.Pin_0, U1.connector2
  N16: U1.connector0, U1.connector1, R7.Pin_0
  N17: U1.connector4, R3.Pin_1, R6.Pin_0
  N18: U1.connector5, U1.connector6, R7.Pin_1, R8.Pin_0, R8.Pin_1, R9.Pin_0, R9.Pin_1
  N19: R5.Pin_0, R6.Pin_1

custom parts:
  Adafruit MCP4725 Breakout Board - 12-Bit DAC: Your microcontroller probably has an ADC (analog -> digital converter) but does it have a DAC (digital -> analog converter)??? Now it can! This breakout board features the easy-to-use MCP4725 12-bit DAC. Control it via I2C and send it the value you want it to output, and the VOUT pin will have it. Great for audio / analog projects, such as when you can't use PWM but need a sine wave or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
  KY-040 Rotary encoder: KY-040 Rotary Encoder with switch on breakout borad from AZ Delivery
  2.8 Zoll LCD IL19341: A generic 2.8 inch LCD TFT 320x240 display with touchscreen and SD card slot. Uses the ILI9341 controller, like the Adafruit displays of this size uses.
